# Fritzing sketch CAM01_quickschema (saved by Fritzing 0.9.3b)
breadboards: 1

parts:
  Part1 = Arduino Pro Mini (3.3V)
  U2 = Battery Holders [package=lipo-1100mAh]
  U4 = mystery part, 2 pins [chip_label=?]
  U5 = Voltage Regulator [package=to220-adj]
  Q1 = MOSFET-NCHANNEL [package=to220v]
  C2 = Ceramic Capacitor [capacitance=100nF package="200 mil [THT, multilayer]"]
  R1 = Resistor [tolerance=±5% resistance=680 package=THT]
  R2 = Resistor [tolerance=±5% resistance=1k package=THT]
  R3 = Resistor [tolerance=±20% resistance=10k package=THT]
  C1_100u = Capacitor Polarized [package=cpol-radial-100uf-25v]
  C3_10u = Capacitor Polarized [package=cpol-radial-10uf-25v]

nets:
  N1: Part1.RAW, U2.+, U5.OUT, C1_100u.-
  N2: Part1.GND, U2.-, Q1.S, C2.0, R2.Pin_0, R3.Pin_0, C1_100u.+, C3_10u.-
  N3: Part1.MISO, Q1.G, R3.Pin_1
  N4: U4.pin2, Q1.D
  N5: U5.ADJ, R1.Pin_0, R2.Pin_1
  N6: U5.IN, C2.1, R1.Pin_1, C3_10u.+
